// Logisim project Circuitos Sequenciais - FSM.circ as structural Verilog: 2 circuits, main circuit Maquina de Estado finito 1111
module Maquina_de_Estado_finito_1111 (
  input  in_1,
  output out_2
);

  wire and_1_out, and_2_out, and_3_out, clock_1_out, d_ff_1_q, d_ff_2_q, d_ff_3_q, not_1_out;

  Clock clock_1 (.out(clock_1_out));
  not not_1 (not_1_out, in_1);
  D_Flip_Flop d_ff_1 (.clk(clock_1_out), .D(in_1), .Q(d_ff_1_q), .en(1'b1));  // open: Qn, preset, reset
  and and_1 (and_1_out, d_ff_1_q, in_1);
  D_Flip_Flop d_ff_2 (.clk(clock_1_out), .D(and_1_out), .Q(d_ff_2_q), .en(1'b1));  // open: Qn, preset, reset
  D_Flip_Flop d_ff_3 (.clk(clock_1_out), .D(and_2_out), .Q(d_ff_3_q), .en(1'b1));  // open: Qn, preset, reset
  and and_2 (and_2_out, d_ff_2_q, in_1);
  and and_3 (and_3_out, d_ff_3_q, in_1);
  D_Flip_Flop d_ff_4 (.clk(clock_1_out), .D(and_3_out), .Q(out_2), .en(1'b1));  // open: Qn, preset, reset
endmodule

module Maquina_de_Mealy (
  input  in_1,
  output out_2
);

  wire and_1_out, and_2_out, and_3_out, clock_1_out, d_ff_1_q, d_ff_2_q, d_ff_3_q, not_1_out;

  Clock clock_1 (.out(clock_1_out));
  not not_1 (not_1_out, in_1);
  D_Flip_Flop d_ff_1 (.clk(clock_1_out), .D(in_1), .Q(d_ff_1_q), .en(1'b1));  // open: Qn, preset, reset
  and and_1 (and_1_out, d_ff_1_q, in_1);
  D_Flip_Flop d_ff_2 (.clk(clock_1_out), .D(and_1_out), .Q(d_ff_2_q), .en(1'b1));  // open: Qn, preset, reset
  and and_2 (and_2_out, d_ff_2_q, not_1_out);
  D_Flip_Flop d_ff_3 (.clk(clock_1_out), .D(and_2_out), .Q(d_ff_3_q), .en(1'b1));  // open: Qn, preset, reset
  and and_3 (and_3_out, d_ff_3_q, in_1);
  D_Flip_Flop d_ff_4 (.clk(clock_1_out), .D(and_3_out), .Q(out_2), .en(1'b1));  // open: Qn, preset, reset

  // Notes on the sheet:
  //   encontra nos estado
  //   Maquina de Mealy a mudança se
  //   Observações: só consegui fazer a máquina de Mealy não foi possível
  //   Fazer a máquina de Moore com meus atuais conhecimentos no Logisim
  //   Sequência da Máquina
  //   1101
  //   Máquina feita com interseções
  //   [110[1]101]
endmodule
