// Logisim project Circuitos Sequenciais - Flip-flops.circ as structural Verilog: 5 circuits, main circuit Contador assíncrono decrescente
module \Contador_assíncrono_decrescente  (
  input  pulse,
  input  x,
  input  clear,
  output out_4,
  output out_5,
  output out_6,
  output out_7,
  output out_8
);

  J_K_Flip_Flop j_k_ff_1 (.J(x), .clk(out_5), .K(x), .Qn(out_4), .reset(clear));  // open: Q, preset, en
  J_K_Flip_Flop j_k_ff_2 (.J(x), .clk(out_6), .K(x), .Qn(out_5), .reset(clear));  // open: Q, preset, en
  J_K_Flip_Flop j_k_ff_3 (.J(x), .clk(out_7), .K(x), .Qn(out_6), .reset(clear));  // open: Q, preset, en
  J_K_Flip_Flop j_k_ff_4 (.J(x), .clk(out_8), .K(x), .Qn(out_7), .reset(clear));  // open: Q, preset, en
  J_K_Flip_Flop j_k_ff_5 (.J(x), .clk(pulse), .K(x), .Qn(out_8), .reset(clear));  // open: Q, preset, en
endmodule

module \Contador_assíncrono_crescente  (
  input  pulse,
  input  x,
  input  clear,
  output out_4,
  output out_5,
  output out_6,
  output out_7,
  output out_8
);

  wire j_k_ff_2_qn, j_k_ff_3_qn, j_k_ff_4_qn, j_k_ff_5_qn;

  J_K_Flip_Flop j_k_ff_1 (.J(x), .clk(j_k_ff_2_qn), .K(x), .Q(out_4), .reset(clear));  // open: Qn, preset, en
  J_K_Flip_Flop j_k_ff_2 (
    .J(x), .clk(j_k_ff_3_qn), .K(x), .Q(out_5), .Qn(j_k_ff_2_qn), .reset(clear));  // open: preset, en
  J_K_Flip_Flop j_k_ff_3 (
    .J(x), .clk(j_k_ff_4_qn), .K(x), .Q(out_6), .Qn(j_k_ff_3_qn), .reset(clear));  // open: preset, en
  J_K_Flip_Flop j_k_ff_4 (
    .J(x), .clk(j_k_ff_5_qn), .K(x), .Q(out_7), .Qn(j_k_ff_4_qn), .reset(clear));  // open: preset, en
  J_K_Flip_Flop j_k_ff_5 (.J(x), .clk(pulse), .K(x), .Q(out_8), .Qn(j_k_ff_5_qn), .reset(clear));  // open: preset, en
endmodule

module \Contador_Decádico_Decrescente  (
  input  in_1,
  input  in_2,
  input  in_3,
  output [4:0] out_4
);

  wire and_1_out, j_k_ff_1_qn, j_k_ff_3_qn, j_k_ff_5_qn, not_1_out, or_1_out;

  not not_1 (not_1_out, in_1);
  and and_1 (and_1_out, j_k_ff_1_qn, out_4[1], j_k_ff_3_qn, out_4[3], j_k_ff_5_qn);
  J_K_Flip_Flop j_k_ff_1 (
    .J(in_1), .clk(in_2), .K(in_1), .Q(out_4[0]), .Qn(j_k_ff_1_qn), .preset(or_1_out), .reset(in_3));  // open: en
  or or_1 (or_1_out, not_1_out, and_1_out);
  J_K_Flip_Flop j_k_ff_2 (
    .J(in_1), .clk(out_4[0]), .K(in_1), .Q(out_4[1]), .preset(or_1_out), .reset(in_3));  // open: Qn, en
  J_K_Flip_Flop j_k_ff_3 (
    .J(in_1), .clk(out_4[1]), .K(in_1), .Q(out_4[2]), .Qn(j_k_ff_3_qn), .preset(or_1_out), .reset(in_3));  // open: en
  J_K_Flip_Flop j_k_ff_4 (
    .J(in_1), .clk(out_4[2]), .K(in_1), .Q(out_4[3]), .preset(or_1_out), .reset(in_3));  // open: Qn, en
  J_K_Flip_Flop j_k_ff_5 (
    .J(in_1), .clk(out_4[3]), .K(in_1), .Q(out_4[4]), .Qn(j_k_ff_5_qn), .preset(or_1_out), .reset(in_3));  // open: en
endmodule

module \Contador_Decádio_Crescente  (
  input  in_1,
  input  in_2,
  input  in_3,
  output [4:0] out_4
);

  wire and_1_out, j_k_ff_1_qn, j_k_ff_2_qn, j_k_ff_3_qn, j_k_ff_4_qn, nand_1_out, not_1_out, not_2_out;

  not not_1 (not_1_out, and_1_out);
  J_K_Flip_Flop j_k_ff_1 (
    .J(in_1), .clk(in_2), .K(in_1), .Q(out_4[0]), .Qn(j_k_ff_1_qn), .reset(nand_1_out));  // open: preset, en
  nand nand_1 (nand_1_out, in_3, not_1_out);
  and and_1 (and_1_out, out_4[0], out_4[1], not_2_out, out_4[3], out_4[4]);
  not not_2 (not_2_out, out_4[2]);
  J_K_Flip_Flop j_k_ff_2 (
    .J(in_1), .clk(j_k_ff_1_qn), .K(in_1), .Q(out_4[1]), .Qn(j_k_ff_2_qn), .reset(nand_1_out));  // open: preset, en
  J_K_Flip_Flop j_k_ff_3 (
    .J(in_1), .clk(j_k_ff_2_qn), .K(in_1), .Q(out_4[2]), .Qn(j_k_ff_3_qn), .reset(nand_1_out));  // open: preset, en
  J_K_Flip_Flop j_k_ff_4 (
    .J(in_1), .clk(j_k_ff_3_qn), .K(in_1), .Q(out_4[3]), .Qn(j_k_ff_4_qn), .reset(nand_1_out));  // open: preset, en
  J_K_Flip_Flop j_k_ff_5 (
    .J(in_1), .clk(j_k_ff_4_qn), .K(in_1), .Q(out_4[4]), .reset(nand_1_out));  // open: Qn, preset, en
endmodule

module Contador_base_10 (
  input  in_1,
  input  in_2,
  output [3:0] out_3
);

  wire and_1_out, not_1_out, or_1_out, t_ff_2_qn, t_ff_3_qn, t_ff_4_qn;

  or or_1 (or_1_out, in_2, and_1_out);
  not not_1 (not_1_out, out_3[2]);
  and and_1 (and_1_out, out_3[3], not_1_out, out_3[1], out_3[0]);
  T_Flip_Flop t_ff_1 (.clk(t_ff_2_qn), .T(t_ff_2_qn), .Q(out_3[3]), .reset(or_1_out));  // open: Qn, preset, en
  T_Flip_Flop t_ff_2 (
    .clk(t_ff_3_qn), .T(t_ff_3_qn), .Q(out_3[2]), .Qn(t_ff_2_qn), .reset(or_1_out));  // open: preset, en
  T_Flip_Flop t_ff_3 (
    .clk(t_ff_4_qn), .T(t_ff_4_qn), .Q(out_3[1]), .Qn(t_ff_3_qn), .reset(or_1_out));  // open: preset, en
  T_Flip_Flop t_ff_4 (.clk(in_1), .T(in_1), .Q(out_3[0]), .Qn(t_ff_4_qn), .reset(or_1_out));  // open: preset, en
endmodule
